// Logisim project CPU8_1411.circ as structural Verilog: 44 circuits, main circuit 01_nand_gate
module _01_nand_gate (
  input  A,
  input  B,
  output Y_buffer,
  output Y_nor,
  output Y_and,
  output Y_or,
  output Y_xor,
  output Y_not,
  output Y_nand,
  output Y_xnor
);

  wire nand_1_out, nand_2_out, nand_3_out, nand_8_out, nand_9_out, nand_10_out, nand_11_out, nand_12_out,
       nand_14_out, nand_15_out, nand_16_out, nand_17_out, nand_18_out, nand_21_out;

  nand nand_1 (nand_1_out, A, B);
  nand nand_2 (nand_2_out, A, A);
  nand nand_3 (nand_3_out, B, B);
  nand nand_4 (Y_and, nand_1_out, nand_1_out);
  nand nand_5 (Y_or, nand_2_out, nand_3_out);
  nand nand_6 (Y_not, A, A);
  nand nand_7 (Y_nand, A, B);
  nand nand_8 (nand_8_out, A, A);
  nand nand_9 (nand_9_out, A, A);
  nand nand_10 (nand_10_out, B, B);
  nand nand_11 (nand_11_out, A, B);
  nand nand_12 (nand_12_out, A, B);
  nand nand_13 (Y_buffer, nand_8_out, nand_8_out);
  nand nand_14 (nand_14_out, nand_9_out, nand_10_out);
  nand nand_15 (nand_15_out, A, nand_11_out);
  nand nand_16 (nand_16_out, nand_11_out, B);
  nand nand_17 (nand_17_out, A, nand_12_out);
  nand nand_18 (nand_18_out, nand_12_out, B);
  nand nand_19 (Y_nor, nand_14_out, nand_14_out);
  nand nand_20 (Y_xor, nand_15_out, nand_16_out);
  nand nand_21 (nand_21_out, nand_17_out, nand_18_out);
  nand nand_22 (Y_xnor, nand_21_out, nand_21_out);
endmodule

module _02_1M (
  input  i,
  input  S,
  output O
);

  wire nand_1_out, nand_2_out, nand_4_out;

  nand nand_1 (nand_1_out, i, S);
  nand nand_2 (nand_2_out, nand_1_out, S);
  nand nand_3 (O, nand_1_out, nand_4_out);
  nand nand_4 (nand_4_out, O, nand_2_out);
endmodule

module _02_1_test (
  input  s,
  input  i,
  input  i_2,
  input  S_2,
  output o,
  output O_2
);

  D_Flip_Flop #(.trigger("high")) d_ff_1 (.clk(s), .D(i), .Q(o));  // open: Qn, preset, reset
  Register #(.trigger("high"), .width(1)) register_1 (.D(i_2), .en(S_2), .Q(O_2), .clk(1'b1));  // open: clr
endmodule

module _03_8Register (
  input  [7:0] i,
  input  set,
  output [7:0] o
);

  Register #(.trigger("high")) register_1 (.D(i), .en(set), .Q(o), .clk(1'b1));  // open: clr
endmodule

module _03_1_Enabler (
  input  [7:0] i,
  input  e,
  output [7:0] out_3
);

  assign out_3 = e ? i : 8'bz;  // Controlled_Buffer controlled_buffer_1
endmodule

module _03_2_8Reg (
  input  [7:0] i,
  input  s,
  input  e,
  output [7:0] o
);

  wire [7:0] n03_8register_1_o;

  _03_8Register u_03_8register_1 (.i(i), .set(s), .o(n03_8register_1_o));
  _03_1_Enabler u_03_1_enabler_1 (.i(n03_8register_1_o), .e(e), .out_3(o));
endmodule

module _03_3_BusTest (
  input  in_1,
  input  in_2,
  input  in_3,
  input  in_4,
  input  [7:0] in_5,
  output [7:0] out_6,
  output [7:0] out_7,
  output [7:0] out_8
);

  wire nor_1_out;

  nor nor_1 (nor_1_out, in_1, in_2);
  assign out_8 = nor_1_out ? in_5 : 8'bz;  // Controlled_Buffer controlled_buffer_1
  _03_2_8Reg RA (.i(out_8), .s(in_3), .e(in_1), .o(out_7));
  assign out_8 = in_1 ? out_7 : 8'bz;  // Controlled_Buffer controlled_buffer_2
  _03_2_8Reg RB (.i(out_8), .s(in_4), .e(in_2), .o(out_6));
  assign out_8 = in_2 ? out_6 : 8'bz;  // Controlled_Buffer controlled_buffer_3
endmodule

module Enabler (
  input  [7:0] i,
  input  e,
  output [7:0] out_3
);

  assign out_3 = e ? i : 8'bz;  // Controlled_Buffer controlled_buffer_1
endmodule

module Adder (
  input  Ci,
  input  [7:0] A,
  input  [7:0] B,
  output [7:0] S,
  output Co
);

  Adder_part adder_1 (.a(A), .b(B), .out(S), .cin(Ci), .cout(Co));
endmodule

module SHR (
  input  [7:0] i,
  input  si,
  output [7:0] o,
  output so
);

  wire [7:1] register_1_q;

  Register #(.trigger("high")) register_1 (.D(i), .en(1'b1), .Q({register_1_q, so}), .clk(1'b1));  // open: clr
  Register #(.trigger("high")) register_2 (.D({si, register_1_q}), .en(1'b1), .Q(o), .clk(1'b1));  // open: clr
endmodule

module SHL (
  input  [7:0] i,
  input  si,
  output [7:0] o,
  output so
);

  wire [6:0] register_1_q;

  Register #(.trigger("high")) register_1 (.D(i), .en(1'b1), .Q({so, register_1_q}), .clk(1'b1));  // open: clr
  Register #(.trigger("high")) register_2 (.D({register_1_q, si}), .en(1'b1), .Q(o), .clk(1'b1));  // open: clr
endmodule

module Invertor (
  input  [7:0] i,
  output [7:0] o
);

  assign o = ~i;  // NOT_Gate not_1, 8 bits wide
endmodule

module Ander (
  input  [7:0] A,
  input  [7:0] B,
  output [7:0] O
);

  assign O = A & B;  // AND_Gate and_1, 8 bits wide
endmodule

module Orer (
  input  [7:0] A,
  input  [7:0] B,
  output [7:0] O
);

  assign O = A | B;  // OR_Gate or_1, 8 bits wide
endmodule

module Xorer1 (
  input  S_I,
  input  L_I,
  input  A,
  input  B,
  output O,
  output S_O,
  output L_O
);

  wire and_2_out, not_1_out;

  xor xor_1 (O, A, B);
  not not_1 (not_1_out, O);
  and and_1 (S_O, not_1_out, S_I);
  and and_2 (and_2_out, S_I, A, O);
  or or_1 (L_O, and_2_out, L_I);
endmodule

module Xorer8 (
  input  [7:0] A,
  input  [7:0] B,
  output [7:0] O,
  output S_O,
  output L_O
);

  wire xorer1_1_l_o, xorer1_1_s_o, xorer1_2_l_o, xorer1_2_s_o, xorer1_3_l_o, xorer1_3_s_o, xorer1_4_l_o,
       xorer1_4_s_o, xorer1_5_l_o, xorer1_5_s_o, xorer1_6_l_o, xorer1_6_s_o, xorer1_7_l_o, xorer1_7_s_o;

  Xorer1 xorer1_1 (.S_I(1'b1), .L_I(1'b0), .A(A[7]), .B(B[7]), .O(O[7]), .S_O(xorer1_1_s_o), .L_O(xorer1_1_l_o));
  Xorer1 xorer1_2 (
    .S_I(xorer1_1_s_o), .L_I(xorer1_1_l_o), .A(A[6]), .B(B[6]), .O(O[6]), .S_O(xorer1_2_s_o),
    .L_O(xorer1_2_l_o));
  Xorer1 xorer1_3 (
    .S_I(xorer1_2_s_o), .L_I(xorer1_2_l_o), .A(A[5]), .B(B[5]), .O(O[5]), .S_O(xorer1_3_s_o),
    .L_O(xorer1_3_l_o));
  Xorer1 xorer1_4 (
    .S_I(xorer1_3_s_o), .L_I(xorer1_3_l_o), .A(A[4]), .B(B[4]), .O(O[4]), .S_O(xorer1_4_s_o),
    .L_O(xorer1_4_l_o));
  Xorer1 xorer1_5 (
    .S_I(xorer1_4_s_o), .L_I(xorer1_4_l_o), .A(A[3]), .B(B[3]), .O(O[3]), .S_O(xorer1_5_s_o),
    .L_O(xorer1_5_l_o));
  Xorer1 xorer1_6 (
    .S_I(xorer1_5_s_o), .L_I(xorer1_5_l_o), .A(A[2]), .B(B[2]), .O(O[2]), .S_O(xorer1_6_s_o),
    .L_O(xorer1_6_l_o));
  Xorer1 xorer1_7 (
    .S_I(xorer1_6_s_o), .L_I(xorer1_6_l_o), .A(A[1]), .B(B[1]), .O(O[1]), .S_O(xorer1_7_s_o),
    .L_O(xorer1_7_l_o));
  Xorer1 xorer1_8 (.S_I(xorer1_7_s_o), .L_I(xorer1_7_l_o), .A(A[0]), .B(B[0]), .O(O[0]), .S_O(S_O), .L_O(L_O));
endmodule

module Zeroer (
  input  [7:0] in,
  output out
);

  nor nor_1 (out, in[0], in[1], in[2], in[3], in[4], in[5], in[6], in[7]);
endmodule

module ALU (
  input  [7:0] A,
  input  [7:0] B,
  input  CI,
  input  [2:0] OP,
  output zero,
  output [7:0] out,
  output CO,
  output A_B,
  output A_B_2
);

  wire adder_1_co, C_AD, C_SL, C_SR, decoder_1_out0, decoder_1_out1, decoder_1_out2, decoder_1_out3,
       decoder_1_out4, decoder_1_out5, decoder_1_out6, decoder_1_out7, shl_1_so, shr_1_so;
  wire [7:0] adder_1_s, ander_1_o, invertor_1_o, orer_1_o, shl_1_o, shr_1_o, xorer8_1_o;

  Adder adder_1 (.Ci(CI), .A(A), .B(B), .S(adder_1_s), .Co(adder_1_co));
  SHR shr_1 (.i(A), .si(CI), .o(shr_1_o), .so(shr_1_so));
  SHL shl_1 (.i(A), .si(CI), .o(shl_1_o), .so(shl_1_so));
  Invertor invertor_1 (.i(A), .o(invertor_1_o));
  Ander ander_1 (.A(A), .B(B), .O(ander_1_o));
  Orer orer_1 (.A(A), .B(B), .O(orer_1_o));
  Xorer8 xorer8_1 (.A(A), .B(B), .O(xorer8_1_o), .S_O(A_B), .L_O(A_B_2));
  Decoder #(.enable("false"), .select(3)) decoder_1 (
    .out0(decoder_1_out0), .out1(decoder_1_out1), .out2(decoder_1_out2), .out3(decoder_1_out3),
    .out4(decoder_1_out4), .out5(decoder_1_out5), .out6(decoder_1_out6), .out7(decoder_1_out7), .sel(OP));
  and and_1 (C_AD, adder_1_co, decoder_1_out0);
  and and_2 (C_SR, shr_1_so, decoder_1_out1);
  and and_3 (C_SL, shl_1_so, decoder_1_out2);
  Enabler enabler_1 (.i(adder_1_s), .e(decoder_1_out0), .out_3(out));
  Enabler enabler_2 (.i(shr_1_o), .e(decoder_1_out1), .out_3(out));
  Enabler enabler_3 (.i(shl_1_o), .e(decoder_1_out2), .out_3(out));
  Enabler enabler_4 (.i(invertor_1_o), .e(decoder_1_out3), .out_3(out));
  Enabler enabler_5 (.i(ander_1_o), .e(decoder_1_out4), .out_3(out));
  Enabler enabler_6 (.i(orer_1_o), .e(decoder_1_out5), .out_3(out));
  Enabler enabler_7 (.i(xorer8_1_o), .e(decoder_1_out6), .out_3(out));
  assign out = decoder_1_out7 ? {8{1'b0}} : 8'bz;  // Controlled_Buffer controlled_buffer_1
  or or_1 (CO, C_AD, C_SR, C_SL);
  Zeroer zeroer_1 (.in(out), .out(zero));
endmodule

module test_ALU (
  input  [7:0] A,
  input  [7:0] B,
  input  CIn,
  input  [2:0] Opcode,
  output [7:0] O,
  output out_6,
  output out_7,
  output out_8,
  output out_9
);

  ALU alu_1 (.A(A), .B(B), .CI(CIn), .OP(Opcode), .zero(out_9), .out(O), .CO(out_6), .A_B(out_8), .A_B_2(out_7));

  // Other names for the same wires on the sheet: CI = CIn; OP[2:0] = Opcode
endmodule

module Stepper (
  input  CLK,
  input  reset,
  output _1,
  output _2,
  output _3,
  output _4,
  output _5,
  output _6,
  output _7
);

  wire d_ff_1_q, d_ff_2_q, d_ff_3_q, d_ff_4_q, d_ff_5_q, d_ff_6_q, d_ff_7_q, d_ff_8_q, d_ff_9_q, d_ff_10_q,
       d_ff_11_q, not_1_out, not_2_out, not_3_out, not_4_out, not_5_out, not_6_out, not_7_out, not_8_out,
       or_1_out, or_2_out;

  not not_1 (not_1_out, CLK);
  not not_2 (not_2_out, _7);
  or or_1 (or_1_out, _7, CLK);
  or or_2 (or_2_out, _7, not_1_out);
  or or_3 (_1, _7, not_3_out);
  D_Flip_Flop d_ff_1 (.clk(or_1_out), .D(not_2_out), .Q(d_ff_1_q), .reset(reset));  // open: Qn, preset
  not not_3 (not_3_out, d_ff_2_q);
  D_Flip_Flop d_ff_2 (.clk(or_2_out), .D(d_ff_1_q), .Q(d_ff_2_q), .reset(reset));  // open: Qn, preset
  and and_1 (_2, d_ff_2_q, not_4_out);
  D_Flip_Flop d_ff_3 (.clk(or_1_out), .D(d_ff_2_q), .Q(d_ff_3_q), .reset(reset));  // open: Qn, preset
  not not_4 (not_4_out, d_ff_4_q);
  D_Flip_Flop d_ff_4 (.clk(or_2_out), .D(d_ff_3_q), .Q(d_ff_4_q), .reset(reset));  // open: Qn, preset
  and and_2 (_3, d_ff_4_q, not_5_out);
  D_Flip_Flop d_ff_5 (.clk(or_1_out), .D(d_ff_4_q), .Q(d_ff_5_q), .reset(reset));  // open: Qn, preset
  not not_5 (not_5_out, d_ff_6_q);
  D_Flip_Flop d_ff_6 (.clk(or_2_out), .D(d_ff_5_q), .Q(d_ff_6_q), .reset(reset));  // open: Qn, preset
  and and_3 (_4, d_ff_6_q, not_6_out);
  D_Flip_Flop d_ff_7 (.clk(or_1_out), .D(d_ff_6_q), .Q(d_ff_7_q), .reset(reset));  // open: Qn, preset
  not not_6 (not_6_out, d_ff_8_q);
  D_Flip_Flop d_ff_8 (.clk(or_2_out), .D(d_ff_7_q), .Q(d_ff_8_q), .reset(reset));  // open: Qn, preset
  and and_4 (_5, d_ff_8_q, not_7_out);
  D_Flip_Flop d_ff_9 (.clk(or_1_out), .D(d_ff_8_q), .Q(d_ff_9_q), .reset(reset));  // open: Qn, preset
  not not_7 (not_7_out, d_ff_10_q);
  D_Flip_Flop d_ff_10 (.clk(or_2_out), .D(d_ff_9_q), .Q(d_ff_10_q), .reset(reset));  // open: Qn, preset
  and and_5 (_6, d_ff_10_q, not_8_out);
  D_Flip_Flop d_ff_11 (.clk(or_1_out), .D(d_ff_10_q), .Q(d_ff_11_q), .reset(reset));  // open: Qn, preset
  not not_8 (not_8_out, _7);
  D_Flip_Flop d_ff_12 (.clk(or_2_out), .D(d_ff_11_q), .Q(_7), .reset(reset));  // open: Qn, preset
endmodule

module test_Stepper (
  output out_1,
  output out_2,
  output out_3,
  output out_4,
  output out_5,
  output out_6,
  output out_7
);

  wire CLK_out;

  Clock CLK (.out(CLK_out));
  Stepper stepper_1 (
    .CLK(CLK_out), .reset(out_7), ._1(out_1), ._2(out_2), ._3(out_3), ._4(out_4), ._5(out_5), ._6(out_6),
    ._7(out_7));
endmodule

module Clk (
  output clk,
  output clk_s,
  output clk_e
);

  wire clk_raw_out, j_k_ff_1_qn;

  Clock clk_raw (.out(clk_raw_out));
  J_K_Flip_Flop j_k_ff_1 (.J(1'b1), .clk(clk_raw_out), .K(1'b1), .Q(clk), .Qn(j_k_ff_1_qn));  // open: preset, reset
  and and_1 (clk_s, clk, clk_raw_out);
  nand nand_1 (clk_e, clk_raw_out, j_k_ff_1_qn);
endmodule

module test_AddControl (
  output TMP_S,
  output R0_E,
  output ACC_S,
  output R1_E,
  output R0_S,
  output ACC_E
);

  wire clk_1_clk, clk_e, clk_s, stepper_1__1, stepper_1__2, stepper_1__3, stepper_1__4, stepper_1__5,
       stepper_1__6, stepper_1__7;

  and and_1 (R0_E, stepper_1__5, clk_e);
  and and_2 (R1_E, stepper_1__4, clk_e);
  and and_3 (ACC_E, stepper_1__6, clk_e);
  Clk clk_1 (.clk(clk_1_clk), .clk_s(clk_s), .clk_e(clk_e));
  LED led_1 (.in(clk_s));
  LED led_2 (.in(clk_e));
  LED led_3 (.in(stepper_1__1));
  LED led_4 (.in(stepper_1__2));
  LED led_5 (.in(stepper_1__3));
  LED led_6 (.in(stepper_1__4));
  LED led_7 (.in(stepper_1__5));
  LED led_8 (.in(stepper_1__6));
  Stepper stepper_1 (
    .CLK(clk_1_clk), .reset(stepper_1__7), ._1(stepper_1__1), ._2(stepper_1__2), ._3(stepper_1__3),
    ._4(stepper_1__4), ._5(stepper_1__5), ._6(stepper_1__6), ._7(stepper_1__7));
  and and_4 (TMP_S, stepper_1__4, clk_s);
  and and_5 (ACC_S, stepper_1__5, clk_s);
  and and_6 (R0_S, stepper_1__6, clk_s);
endmodule

module R0 (
  input  [7:0] i,
  input  s,
  input  e,
  output [7:0] o
);

  wire [7:0] register_1_q;

  Register #(.trigger("high")) register_1 (.D(i), .en(s), .Q(register_1_q), .clk(1'b1));  // open: clr
  _03_1_Enabler u_03_1_enabler_1 (.i(register_1_q), .e(e), .out_3(o));
endmodule

module R1 (
  input  [7:0] i,
  input  s,
  input  e,
  output [7:0] o
);

  wire [7:0] register_1_q;

  Register #(.trigger("high")) register_1 (.D(i), .en(s), .Q(register_1_q), .clk(1'b1));  // open: clr
  _03_1_Enabler u_03_1_enabler_1 (.i(register_1_q), .e(e), .out_3(o));
endmodule

module TMP (
  input  [7:0] i,
  input  s,
  input  e,
  output [7:0] o
);

  wire [7:0] register_1_q;

  Register #(.trigger("high")) register_1 (.D(i), .en(s), .Q(register_1_q), .clk(1'b1));  // open: clr
  _03_1_Enabler u_03_1_enabler_1 (.i(register_1_q), .e(e), .out_3(o));
endmodule

module ACC (
  input  [7:0] i,
  input  s,
  input  e,
  output [7:0] o
);

  wire [7:0] register_1_q;

  Register #(.trigger("high")) register_1 (.D(i), .en(s), .Q(register_1_q), .clk(1'b1));  // open: clr
  _03_1_Enabler u_03_1_enabler_1 (.i(register_1_q), .e(e), .out_3(o));
endmodule

module test_AddCOMPUTER (
  output [7:0] out_1
);

  wire test_addcontrol_1_acc_e, test_addcontrol_1_acc_s, test_addcontrol_1_r0_e, test_addcontrol_1_r0_s,
       test_addcontrol_1_r1_e, test_addcontrol_1_tmp_s;
  wire [7:0] alu_1_out, tmp_1_o;

  ALU alu_1 (.A(out_1), .B(tmp_1_o), .out(alu_1_out));  // open: CI, OP, zero, CO, A_B, A_B_2
  ACC acc_1 (.i(alu_1_out), .s(test_addcontrol_1_acc_s), .e(test_addcontrol_1_acc_e), .o(out_1));
  TMP tmp_1 (.i(out_1), .s(test_addcontrol_1_tmp_s), .e(1'b1), .o(tmp_1_o));
  R0 r0_1 (.i(out_1), .s(test_addcontrol_1_r0_s), .e(test_addcontrol_1_r0_e), .o(out_1));
  R1 r1_1 (.i(out_1), .e(test_addcontrol_1_r1_e), .o(out_1));  // open: s
  test_AddControl test_addcontrol_1 (
    .TMP_S(test_addcontrol_1_tmp_s), .R0_E(test_addcontrol_1_r0_e), .ACC_S(test_addcontrol_1_acc_s),
    .R1_E(test_addcontrol_1_r1_e), .R0_S(test_addcontrol_1_r0_s), .ACC_E(test_addcontrol_1_acc_e));
endmodule

module R2 (
  input  [7:0] i,
  input  s,
  input  e,
  output [7:0] o
);

  wire [7:0] register_1_q;

  Register #(.trigger("high")) register_1 (.D(i), .en(s), .Q(register_1_q), .clk(1'b1));  // open: clr
  _03_1_Enabler u_03_1_enabler_1 (.i(register_1_q), .e(e), .out_3(o));
endmodule

module R3 (
  input  [7:0] i,
  input  s,
  input  e,
  output [7:0] o
);

  wire [7:0] register_1_q;

  Register #(.trigger("high")) register_1 (.D(i), .en(s), .Q(register_1_q), .clk(1'b1));  // open: clr
  _03_1_Enabler u_03_1_enabler_1 (.i(register_1_q), .e(e), .out_3(o));
endmodule

module TMP1 (
  input  [7:0] i,
  input  s,
  output [7:0] o
);

  Register #(.trigger("high")) register_1 (.D(i), .en(s), .Q(o), .clk(1'b1));  // open: clr
endmodule

module ACC1 (
  input  [7:0] i,
  input  s,
  input  e,
  output [7:0] o
);

  wire [7:0] register_1_q;

  Register #(.trigger("high")) register_1 (.D(i), .en(s), .Q(register_1_q), .clk(1'b1));  // open: clr
  _03_1_Enabler u_03_1_enabler_1 (.i(register_1_q), .e(e), .out_3(o));
endmodule

module test_COMPUTER (
  output [7:0] out_1
);

  wire test_addcontrol_1_acc_e, test_addcontrol_1_acc_s, test_addcontrol_1_r0_e, test_addcontrol_1_r0_s,
       test_addcontrol_1_r1_e, test_addcontrol_1_tmp_s;
  wire [7:0] alu_1_out, tmp1_1_o;

  TMP1 tmp1_1 (.i(out_1), .s(test_addcontrol_1_tmp_s), .o(tmp1_1_o));
  ALU alu_1 (.A(out_1), .B(tmp1_1_o), .out(alu_1_out));  // open: CI, OP, zero, CO, A_B, A_B_2
  ACC1 acc1_1 (.i(alu_1_out), .s(test_addcontrol_1_acc_s), .e(test_addcontrol_1_acc_e), .o(out_1));
  R0 r0_1 (.i(out_1), .s(test_addcontrol_1_r0_s), .e(test_addcontrol_1_r0_e), .o(out_1));
  R1 r1_1 (.i(out_1), .e(test_addcontrol_1_r1_e), .o(out_1));  // open: s
  R2 r2_1 (.i(out_1), .o(out_1));  // open: s, e
  test_AddControl test_addcontrol_1 (
    .TMP_S(test_addcontrol_1_tmp_s), .R0_E(test_addcontrol_1_r0_e), .ACC_S(test_addcontrol_1_acc_s),
    .R1_E(test_addcontrol_1_r1_e), .R0_S(test_addcontrol_1_r0_s), .ACC_E(test_addcontrol_1_acc_e));
  R3 r3_1 (.i(out_1), .o(out_1));  // open: s, e
endmodule

module MAR (
  input  [7:0] i,
  input  s,
  output [7:0] o
);

  Register #(.trigger("high")) register_1 (.D(i), .en(s), .Q(o), .clk(1'b1));  // open: clr
endmodule

module RAM (
  input  [7:0] a,
  input  sa,
  input  s,
  input  [7:0] i,
  input  e,
  output [7:0] o
);

  wire [7:0] controlled_buffer_1_out, mar_1_o, ram_1_dout;

  MAR mar_1 (.i(a), .s(sa), .o(mar_1_o));
  assign controlled_buffer_1_out = s ? i : 8'bz;  // Controlled_Buffer controlled_buffer_1
  assign o = e ? ram_1_dout : 8'bz;  // Controlled_Buffer controlled_buffer_2
  Hex_Digit_Display hex_digit_display_1 (.value(mar_1_o[7:4]));  // open: dp
  RAM_part #(.trigger("high")) ram_1 (
    .addr(mar_1_o), .we(s), .clk(1'b1), .din(controlled_buffer_1_out), .dout(ram_1_dout));
  Hex_Digit_Display hex_digit_display_2 (.value(mar_1_o[3:0]));  // open: dp
  Hex_Digit_Display hex_digit_display_3 (.value(ram_1_dout[7:4]));  // open: dp
  Hex_Digit_Display hex_digit_display_4 (.value(ram_1_dout[3:0]));  // open: dp
endmodule

module IAR (
  input  [7:0] i,
  input  s,
  input  e,
  output [7:0] o
);

  wire [7:0] register_1_q;

  Register #(.trigger("high")) register_1 (.D(i), .en(s), .Q(register_1_q), .clk(1'b1));  // open: clr
  _03_1_Enabler u_03_1_enabler_1 (.i(register_1_q), .e(e), .out_3(o));
endmodule

module IR (
  input  [7:0] i,
  input  s,
  output _0,
  output _1,
  output _2,
  output _3,
  output _4,
  output _5,
  output _6,
  output _7
);

  Register #(.trigger("high")) register_1 (
    .D(i), .en(s), .Q({_7, _6, _5, _4, _3, _2, _1, _0}), .clk(1'b1));  // open: clr
endmodule

module Bus1 (
  input  [7:0] i,
  input  bus1_e,
  output [7:0] o
);

  wire not_1_out;

  not not_1 (not_1_out, bus1_e);
  assign o = not_1_out ? i : 8'bz;  // Controlled_Buffer controlled_buffer_1
  assign o = bus1_e ? 8'h1 : 8'bz;  // Controlled_Buffer controlled_buffer_2
endmodule

module CTMP (
  input  i,
  input  s,
  input  e,
  output o
);

  wire register_1_q;

  Register #(.trigger("high"), .width(1)) register_1 (.D(i), .en(s), .Q(register_1_q), .clk(1'b1));  // open: clr
  and and_1 (o, register_1_q, e);
endmodule

module Flags (
  input  i_4,
  input  i_5,
  input  i_6,
  input  i_7,
  input  s,
  output o_4,
  output o_5,
  output o_6,
  output o_7
);

  wire [3:0] register_1_q;

  Register #(.trigger("high")) register_1 (
    .D({i_7, i_6, i_5, i_4, 4'b0000}), .en(s), .Q({o_7, o_6, o_5, o_4, register_1_q}), .clk(1'b1));  // open: clr
endmodule

module ControlUnit1 (
  input  F4,
  input  F5,
  input  F6,
  input  F7,
  input  _0,
  input  _1,
  input  _2,
  input  _3,
  input  _4,
  input  _5,
  input  _6,
  input  _7,
  output BUS1_E,
  output MAR_S,
  output R0_E,
  output R0_S,
  output IAR_E,
  output IR_S,
  output R1_E,
  output R1_S,
  output RAM_E,
  output IAR_S,
  output R2_E,
  output R2_S,
  output ACC_E,
  output ACC_S,
  output R3_E,
  output R3_S,
  output TMP_S,
  output RAM_S,
  output CI_E,
  output FLAGS_S,
  output [2:0] op_out
);

  wire clk_1_clk, clk_e, clk_s, S1, S2, S3, S4, S5, S6, stepper_1__7;

  Clk clk_1 (.clk(clk_1_clk), .clk_s(clk_s), .clk_e(clk_e));
  LED led_1 (.in(clk_e));
  LED led_2 (.in(S1));
  LED led_3 (.in(S2));
  LED led_4 (.in(S3));
  LED led_5 (.in(S4));
  LED led_6 (.in(S5));
  Stepper stepper_1 (
    .CLK(clk_1_clk), .reset(stepper_1__7), ._1(S1), ._2(S2), ._3(S3), ._4(S4), ._5(S5), ._6(S6),
    ._7(stepper_1__7));
  LED led_7 (.in(S6));
  LED led_8 (.in(clk_s));

  // Notes on the sheet:
  //   [ Stepper Module ]
  //   [ IR Code Module ]
endmodule

module COMPUTER1 (
  output [7:0] out_1
);

  wire test_addcontrol_1_acc_e, test_addcontrol_1_acc_s, test_addcontrol_1_r0_e, test_addcontrol_1_r0_s,
       test_addcontrol_1_r1_e, test_addcontrol_1_tmp_s;
  wire [7:0] alu_1_out, tmp1_1_o;

  TMP1 tmp1_1 (.i(out_1), .s(test_addcontrol_1_tmp_s), .o(tmp1_1_o));
  ALU alu_1 (.A(out_1), .B(tmp1_1_o), .out(alu_1_out));  // open: CI, OP, zero, CO, A_B, A_B_2
  ACC1 acc1_1 (.i(alu_1_out), .s(test_addcontrol_1_acc_s), .e(test_addcontrol_1_acc_e), .o(out_1));
  R0 r0_1 (.i(out_1), .s(test_addcontrol_1_r0_s), .e(test_addcontrol_1_r0_e), .o(out_1));
  R1 r1_1 (.i(out_1), .e(test_addcontrol_1_r1_e), .o(out_1));  // open: s
  R2 r2_1 (.i(out_1), .o(out_1));  // open: s, e
  test_AddControl test_addcontrol_1 (
    .TMP_S(test_addcontrol_1_tmp_s), .R0_E(test_addcontrol_1_r0_e), .ACC_S(test_addcontrol_1_acc_s),
    .R1_E(test_addcontrol_1_r1_e), .R0_S(test_addcontrol_1_r0_s), .ACC_E(test_addcontrol_1_acc_e));
  R3 r3_1 (.i(out_1), .o(out_1));  // open: s, e
endmodule

module ControlUnit2 (
  input  _0,
  input  _1,
  input  _2,
  input  _3,
  input  _4,
  input  _5,
  input  _6,
  input  _7,
  input  F4,
  input  F5,
  input  F6,
  input  F7,
  output BUS1_E,
  output MAR_S,
  output IAR_E,
  output IR_S,
  output RAM_E,
  output IAR_S,
  output ACC_E,
  output ACC_S,
  output [2:0] op_out,
  output TMP_S,
  output RAM_S,
  output CI_E,
  output FLAGS_S,
  output R0_S,
  output R0_E,
  output R1_S,
  output R1_E,
  output R2_S,
  output R2_E,
  output R3_S,
  output R3_E
);

  wire ACC_ALU_E, ACC_ALU_S, ACC_IF_E, ACC_IF_S, and_1_out, and_2_out, and_3_out, and_4_out, and_5_out,
       and_6_out, and_7_out, and_8_out, BUS1_IF_E, CL_ALU_E, CLF_E, clk_1_clk, clk_e, clk_s, DATA_E,
       decoder_1_out0, decoder_1_out1, decoder_1_out2, decoder_1_out3, decoder_2_out0, decoder_2_out1,
       decoder_2_out2, decoder_2_out3, decoder_3_out0, decoder_3_out1, decoder_3_out2, decoder_3_out3,
       decoder_4_out0, decoder_4_out1, decoder_4_out2, decoder_4_out3, decoder_4_out4, decoder_4_out5,
       decoder_4_out6, IAR_IF_E, IAR_IF_S, IR_IF_S, JC_E, JMP_E, JMPR_E, LD_E, MAR_IF_S, NOP_E, not_1_out,
       RA_E, RAM_IF_E, RB_ALU_E, RB_ALU_S, RB_E, RB_S, S1, S2, S2_IF, S3, S3_IF, S3IF, S4, S4_ALU, S5,
       S5_ALU, S6, S6_ALU, ST_E, stepper_1__7, TMP_ALU_S, UPDATE_RB;

  or or_1 (BUS1_E, 1'b0, 1'b0, 1'b0, 1'b0, 1'b0, 1'b0, 1'b0, 1'b0);
  or or_2 (IAR_E, 1'b0, 1'b0, 1'b0, 1'b0, 1'b0, 1'b0, 1'b0, 1'b0);
  or or_3 (RAM_E, 1'b0, 1'b0, 1'b0, 1'b0, 1'b0, 1'b0, 1'b0, 1'b0);
  or or_4 (ACC_E, ACC_ALU_E, 1'b0, 1'b0, 1'b0, 1'b0, 1'b0, 1'b0, 1'b0);
  or or_5 (RA_E, CL_ALU_E, 1'b0, 1'b0, 1'b0, 1'b0, 1'b0, 1'b0, 1'b0);
  or or_6 (RB_E, RB_ALU_E, 1'b0, 1'b0, 1'b0, 1'b0, 1'b0, 1'b0, 1'b0);
  or or_7 (CI_E, CL_ALU_E, CL_ALU_E);
  Clk clk_1 (.clk(clk_1_clk), .clk_s(clk_s), .clk_e(clk_e));
  LED led_1 (.in(clk_e));
  LED led_2 (.in(S1));
  LED led_3 (.in(S2));
  LED led_4 (.in(S3));
  LED led_5 (.in(S4));
  LED led_6 (.in(S5));
  Stepper stepper_1 (
    .CLK(clk_1_clk), .reset(stepper_1__7), ._1(S1), ._2(S2), ._3(S3), ._4(S4), ._5(S5), ._6(S6),
    ._7(stepper_1__7));
  LED led_7 (.in(S6));
  LED led_8 (.in(clk_s));
  or or_8 (MAR_S, 1'b0, 1'b0, 1'b0, 1'b0, 1'b0, 1'b0, 1'b0, 1'b0);
  or or_9 (IR_S, 1'b0, 1'b0, 1'b0, 1'b0, 1'b0, 1'b0, 1'b0, 1'b0);
  or or_10 (IAR_S, 1'b0, 1'b0, 1'b0, 1'b0, 1'b0, 1'b0, 1'b0, 1'b0);
  or or_11 (ACC_S, ACC_ALU_S, 1'b0, 1'b0, 1'b0, 1'b0, 1'b0, 1'b0, 1'b0);
  or or_12 (TMP_S, TMP_ALU_S, 1'b0, 1'b0, 1'b0, 1'b0, 1'b0, 1'b0, 1'b0);
  // OR_Gate or_13 has open pins: in0=ACC_ALU_S, in1=1'b0, in2=1'b0, in3=1'b0, in4=1'b0, in5=1'b0, in6=1'b0, in7=1'b0, out=open
  or or_14 (RB_S, RB_ALU_S, 1'b0, 1'b0, 1'b0, 1'b0, 1'b0, 1'b0, 1'b0);
  or or_15 (FLAGS_S, 1'b0, 1'b0);
  or or_16 (R0_E, and_1_out, and_5_out);
  or or_17 (R1_E, and_2_out, and_6_out);
  or or_18 (R2_E, and_3_out, and_7_out);
  or or_19 (R3_E, and_4_out, and_8_out);
  and and_1 (and_1_out, clk_e, RB_E, decoder_1_out0);
  and and_2 (and_2_out, clk_e, RB_E, decoder_1_out1);
  and and_3 (and_3_out, clk_e, RB_E, decoder_1_out2);
  and and_4 (and_4_out, clk_e, RB_E, decoder_1_out3);
  and and_5 (and_5_out, clk_e, RA_E, decoder_2_out0);
  and and_6 (and_6_out, clk_e, RA_E, decoder_2_out1);
  and and_7 (and_7_out, clk_e, RA_E, decoder_2_out2);
  and and_8 (and_8_out, clk_e, RA_E, decoder_2_out3);
  and and_9 (op_out[0], S5_ALU, _0, _3);
  and and_10 (op_out[1], S5_ALU, _0, _2);
  and and_11 (op_out[2], S5_ALU, _0, _1);
  and and_12 (S4_ALU, S4, _0);
  and and_13 (S5_ALU, S5, _0);
  and and_14 (S6_ALU, S6, _0, UPDATE_RB);
  Decoder #(.enable("false"), .select(2)) decoder_1 (
    .out0(decoder_1_out0), .out1(decoder_1_out1), .out2(decoder_1_out2), .out3(decoder_1_out3), .sel({_6, _7}));
  Decoder #(.enable("false"), .select(2)) decoder_2 (
    .out0(decoder_2_out0), .out1(decoder_2_out1), .out2(decoder_2_out2), .out3(decoder_2_out3), .sel({_4, _5}));
  and and_15 (BUS1_IF_E, S1, NOP_E);
  and and_16 (S2_IF, S2, NOP_E);
  and and_17 (S3_IF, S3, NOP_E);
  Decoder #(.enable("false"), .select(2)) decoder_3 (
    .out0(decoder_3_out0), .out1(decoder_3_out1), .out2(decoder_3_out2), .out3(decoder_3_out3), .sel({_6, _7}));
  not not_1 (not_1_out, _0);
  Decoder #(.enable("false"), .select(3)) decoder_4 (
    .out0(decoder_4_out0), .out1(decoder_4_out1), .out2(decoder_4_out2), .out3(decoder_4_out3),
    .out4(decoder_4_out4), .out5(decoder_4_out5), .out6(decoder_4_out6), .sel({_1, _2, _3}));  // open: out7
  nand nand_1 (UPDATE_RB, _3, _2, _1);
  and and_18 (RB_ALU_E, clk_e, S4_ALU);
  and and_19 (CL_ALU_E, clk_e, S5_ALU);
  and and_20 (ACC_ALU_E, clk_e, S6_ALU);
  and and_21 (IAR_IF_E, clk_e, BUS1_IF_E);
  and and_22 (RAM_IF_E, clk_e, S2_IF);
  and and_23 (ACC_IF_E, clk_e, S3IF);
  and and_24 (R0_S, clk_s, RB_S, decoder_3_out0);
  and and_25 (R1_S, clk_s, RB_S, decoder_3_out1);
  and and_26 (R2_S, clk_s, RB_S, decoder_3_out2);
  and and_27 (R3_S, clk_s, RB_S, decoder_3_out3);
  and and_28 (LD_E, not_1_out, decoder_4_out0);
  and and_29 (ST_E, not_1_out, decoder_4_out1);
  and and_30 (DATA_E, not_1_out, decoder_4_out2);
  and and_31 (JMPR_E, not_1_out, decoder_4_out3);
  and and_32 (JMP_E, not_1_out, decoder_4_out4);
  and and_33 (JC_E, not_1_out, decoder_4_out5);
  buf and_34 (CLF_E, not_1_out);  // AND_Gate
  and and_35 (NOP_E, not_1_out, decoder_4_out6);
  and and_36 (TMP_ALU_S, clk_s, S4_ALU);
  and and_37 (ACC_ALU_S, clk_s, S5_ALU);
  and and_38 (RB_ALU_S, clk_s, S6_ALU);
  and and_39 (ACC_IF_S, clk_s, BUS1_IF_E);
  and and_40 (MAR_IF_S, clk_s, BUS1_IF_E);
  and and_41 (IR_IF_S, clk_s, S2_IF);
  and and_42 (IAR_IF_S, clk_s, S3IF);
  // also tied to GND on the sheet: CL_ALU_E

  // Other names for the same wires on the sheet: IR_5 = _5; IR_4 = _4; IR_7 = _7; IR_6 = _6; IR_3 = _3; IR_2 = _2;
  //   IR_1 = _1; FLAGS_ALU_S = ACC_ALU_S; IR_0 = _0; RA_ALU_E = CL_ALU_E; S1_IF = BUS1_IF_E

  // Notes on the sheet:
  //   [ Stepper Module ]
  //   [ ALU Instruction Condition]
  //   [ Instruction Fetch Condition]
  //   [ IR Code Module ]
  //   [ Register Selection Module ]
  //   [ NON_ALU Instruction Condition ]
  //   [ ALU Instruction Module]
  //   [Instruction Fetch Module]
endmodule

module COMPUTER2 (
  output [7:0] out_1
);

  wire alu_1_a_b, alu_1_a_b_2, alu_1_co, alu_1_zero, controlunit2_1_acc_e, controlunit2_1_acc_s,
       controlunit2_1_bus1_e, controlunit2_1_ci_e, controlunit2_1_flags_s, controlunit2_1_iar_e,
       controlunit2_1_iar_s, controlunit2_1_ir_s, controlunit2_1_mar_s, controlunit2_1_r0_e,
       controlunit2_1_r0_s, controlunit2_1_r1_e, controlunit2_1_r1_s, controlunit2_1_r2_e,
       controlunit2_1_r2_s, controlunit2_1_r3_e, controlunit2_1_r3_s, controlunit2_1_ram_e,
       controlunit2_1_ram_s, controlunit2_1_tmp_s, ctmp_1_o, flags_1_o_4, flags_1_o_5, flags_1_o_6,
       flags_1_o_7, ir_1__0, ir_1__1, ir_1__2, ir_1__3, ir_1__4, ir_1__5, ir_1__6, ir_1__7;
  wire [2:0] controlunit2_1_op_out;
  wire [7:0] alu_1_out, bus1_1_o, tmp1_1_o;

  TMP1 tmp1_1 (.i(out_1), .s(controlunit2_1_tmp_s), .o(tmp1_1_o));
  Bus1 bus1_1 (.i(tmp1_1_o), .bus1_e(controlunit2_1_bus1_e), .o(bus1_1_o));
  ALU alu_1 (
    .A(out_1), .B(bus1_1_o), .CI(ctmp_1_o), .OP(controlunit2_1_op_out), .zero(alu_1_zero), .out(alu_1_out),
    .CO(alu_1_co), .A_B(alu_1_a_b), .A_B_2(alu_1_a_b_2));
  ACC1 acc1_1 (.i(alu_1_out), .s(controlunit2_1_acc_s), .e(controlunit2_1_acc_e), .o(out_1));
  CTMP ctmp_1 (.s(controlunit2_1_tmp_s), .i(flags_1_o_4), .e(controlunit2_1_ci_e), .o(ctmp_1_o));
  Flags flags_1 (
    .s(controlunit2_1_flags_s), .i_4(alu_1_co), .i_5(alu_1_a_b_2), .i_6(alu_1_a_b), .i_7(alu_1_zero),
    .o_4(flags_1_o_4), .o_5(flags_1_o_5), .o_6(flags_1_o_6), .o_7(flags_1_o_7));
  R0 r0_1 (.i(out_1), .s(controlunit2_1_r0_s), .e(controlunit2_1_r0_e), .o(out_1));
  R1 r1_1 (.i(out_1), .s(controlunit2_1_r1_s), .e(controlunit2_1_r1_e), .o(out_1));
  IAR iar_1 (.s(controlunit2_1_iar_s), .e(controlunit2_1_iar_e));  // open: i, o
  IR ir_1 (
    .i(out_1), .s(controlunit2_1_ir_s), ._0(ir_1__0), ._1(ir_1__1), ._2(ir_1__2), ._3(ir_1__3), ._4(ir_1__4),
    ._5(ir_1__5), ._6(ir_1__6), ._7(ir_1__7));
  R2 r2_1 (.i(out_1), .s(controlunit2_1_r2_s), .e(controlunit2_1_r2_e), .o(out_1));
  R3 r3_1 (.i(out_1), .s(controlunit2_1_r3_s), .e(controlunit2_1_r3_e), .o(out_1));
  ControlUnit2 controlunit2_1 (
    ._0(ir_1__0), ._1(ir_1__1), ._2(ir_1__2), ._3(ir_1__3), ._4(ir_1__4), ._5(ir_1__5), ._6(ir_1__6),
    ._7(ir_1__7), .op_out(controlunit2_1_op_out), .BUS1_E(controlunit2_1_bus1_e),
    .IAR_E(controlunit2_1_iar_e), .RAM_E(controlunit2_1_ram_e), .ACC_E(controlunit2_1_acc_e),
    .CI_E(controlunit2_1_ci_e), .MAR_S(controlunit2_1_mar_s), .IR_S(controlunit2_1_ir_s),
    .IAR_S(controlunit2_1_iar_s), .ACC_S(controlunit2_1_acc_s), .TMP_S(controlunit2_1_tmp_s),
    .RAM_S(controlunit2_1_ram_s), .FLAGS_S(controlunit2_1_flags_s), .R0_E(controlunit2_1_r0_e),
    .R0_S(controlunit2_1_r0_s), .R1_E(controlunit2_1_r1_e), .R1_S(controlunit2_1_r1_s),
    .R2_E(controlunit2_1_r2_e), .R2_S(controlunit2_1_r2_s), .R3_E(controlunit2_1_r3_e),
    .R3_S(controlunit2_1_r3_s), .F4(flags_1_o_4), .F5(flags_1_o_5), .F6(flags_1_o_6), .F7(flags_1_o_7));
  RAM ram_1 (
    .a(out_1), .sa(controlunit2_1_mar_s), .s(controlunit2_1_ram_s), .i(out_1), .e(controlunit2_1_ram_e),
    .o(out_1));
endmodule
