// Logisim project JOB01_1411.circ as structural Verilog: 2 circuits, main circuit main
module main (
);

  wire clock_1_out, clock_2_out;

  Clock #(.highDuration(2), .lowDuration(2)) clock_1 (.out(clock_1_out));
  Clock clock_2 (.out(clock_2_out));
  _01_basic_gates u_01_basic_gates_1 (
    .A(clock_1_out), .B(clock_2_out));  // open: Y_and, Y_or, Y_not, Y_nand, Y_nor, Y_xor, Y_xnor, Y_buffer
endmodule

module _01_basic_gates (
  input  A,
  input  B,
  output Y_and,
  output Y_or,
  output Y_not,
  output Y_nand,
  output Y_nor,
  output Y_xor,
  output Y_xnor,
  output Y_buffer
);

  and and_1 (Y_and, A, B);
  or or_1 (Y_or, A, B);
  not not_1 (Y_not, A);
  nand nand_1 (Y_nand, A, B);
  nor nor_1 (Y_nor, A, B);
  xor xor_1 (Y_xor, A, B);
  xnor xnor_1 (Y_xnor, A, B);
  buf buffer_1 (Y_buffer, A);
  LED led_1 (.in(Y_and));
  LED led_2 (.in(Y_or));
  LED led_3 (.in(Y_not));
  LED led_4 (.in(Y_nand));
  LED led_5 (.in(Y_nor));
  LED led_6 (.in(Y_xor));
  LED led_7 (.in(Y_xnor));
  LED led_8 (.in(Y_buffer));

  // Notes on the sheet:
  //   basic logic gates
endmodule
