// Logisim project JOB03_1411.circ as structural Verilog: 9 circuits, main circuit main
module main (
);

  wire clock_1_out, clock_2_out;

  Clock #(.highDuration(2), .lowDuration(2)) clock_1 (.out(clock_1_out));
  Clock clock_2 (.out(clock_2_out));
  _01_basic_gates u_01_basic_gates_1 (
    .A(clock_1_out), .B(clock_2_out));  // open: Y_and, Y_or, Y_not, Y_nand, Y_nor, Y_xor, Y_xnor, Y_buffer
endmodule

module _01_basic_gates (
  input  A,
  input  B,
  output Y_and,
  output Y_or,
  output Y_not,
  output Y_nand,
  output Y_nor,
  output Y_xor,
  output Y_xnor,
  output Y_buffer
);

  and and_1 (Y_and, A, B);
  or or_1 (Y_or, A, B);
  not not_1 (Y_not, A);
  nand nand_1 (Y_nand, A, B);
  nor nor_1 (Y_nor, A, B);
  xor xor_1 (Y_xor, A, B);
  xnor xnor_1 (Y_xnor, A, B);
  buf buffer_1 (Y_buffer, A);
  LED led_1 (.in(Y_and));
  LED led_2 (.in(Y_or));
  LED led_3 (.in(Y_not));
  LED led_4 (.in(Y_nand));
  LED led_5 (.in(Y_nor));
  LED led_6 (.in(Y_xor));
  LED led_7 (.in(Y_xnor));
  LED led_8 (.in(Y_buffer));

  // Notes on the sheet:
  //   basic logic gates
endmodule

module _02_HA (
  input  A,
  input  B,
  output S,
  output C
);

  xor xor_1 (S, A, B);
  and and_1 (C, A, B);
endmodule

module _03_FA (
  input  A,
  input  B,
  input  Z,
  output S,
  output C
);

  wire n02_ha_1_c, n02_ha_1_s, n02_ha_2_c;

  _02_HA u_02_ha_1 (.A(A), .B(B), .S(n02_ha_1_s), .C(n02_ha_1_c));
  _02_HA u_02_ha_2 (.A(n02_ha_1_s), .B(Z), .S(S), .C(n02_ha_2_c));
  or or_1 (C, n02_ha_2_c, n02_ha_1_c);
endmodule

module _04_Add_4bits (
  input  [3:0] A,
  input  [3:0] B,
  output [3:0] S,
  output C
);

  wire n03_fa_1_p5, n03_fa_2_p5, n03_fa_3_p5;

  // _03_FA 03_fa_1: pin names not known; wires that end beside it: A[0], B[0], 1'b0, S[0], n03_fa_1_p5
  // _03_FA 03_fa_2: pin names not known; wires that end beside it: A[1], B[1], n03_fa_1_p5, S[1], n03_fa_2_p5
  // _03_FA 03_fa_3: pin names not known; wires that end beside it: A[2], B[2], n03_fa_2_p5, S[2], n03_fa_3_p5
  // _03_FA 03_fa_4: pin names not known; wires that end beside it: A[3], B[3], n03_fa_3_p5, S[3], C

  // Notes on the sheet:
  //   0th
  //   1th
  //   2th
  //   3th
endmodule

module _05_HS (
  input  A,
  input  B,
  output D,
  output Br
);

  wire not_1_out;

  xor xor_1 (D, A, B);
  not not_1 (not_1_out, A);
  and and_1 (Br, not_1_out, B);
endmodule

module _06_FS (
  input  A,
  input  B,
  input  Z,
  output S,
  output C
);

  wire n05_hs_1_br, n05_hs_1_d, n05_hs_2_br;

  _05_HS u_05_hs_1 (.A(A), .B(B), .D(n05_hs_1_d), .Br(n05_hs_1_br));
  _05_HS u_05_hs_2 (.A(n05_hs_1_d), .B(Z), .D(S), .Br(n05_hs_2_br));
  or or_1 (C, n05_hs_2_br, n05_hs_1_br);
endmodule

module _07_Sub_4bits (
  input  [3:0] A,
  input  [3:0] B,
  output [3:0] S,
  output C
);

  wire n06_fs_1_c, n06_fs_2_c, n06_fs_3_c;

  _06_FS u_06_fs_1 (.A(A[0]), .B(B[0]), .Z(1'b0), .S(S[0]), .C(n06_fs_1_c));
  _06_FS u_06_fs_2 (.A(A[1]), .B(B[1]), .Z(n06_fs_1_c), .S(S[1]), .C(n06_fs_2_c));
  _06_FS u_06_fs_3 (.A(A[2]), .B(B[2]), .Z(n06_fs_2_c), .S(S[2]), .C(n06_fs_3_c));
  _06_FS u_06_fs_4 (.A(A[3]), .B(B[3]), .Z(n06_fs_3_c), .S(S[3]), .C(C));

  // Other names for the same wires on the sheet: d0 = S[0]; d1 = S[1]; d2 = S[2]; d3 = S[3]

  // Notes on the sheet:
  //   0th
  //   1th
  //   2th
  //   3th
endmodule

module _08_add_sub_4bits (
  input  [3:0] A,
  input  [3:0] B,
  input  sign,
  output [3:0] S,
  output C
);

  wire B0, B1, B2, B3, n03_fa_1_c, n03_fa_2_c, n03_fa_3_c;

  _03_FA u_03_fa_1 (.A(A[0]), .B(B0), .Z(sign), .S(S[0]), .C(n03_fa_1_c));
  xor xor_1 (B0, B[0], sign);
  xor xor_2 (B1, B[1], sign);
  xor xor_3 (B2, B[2], sign);
  xor xor_4 (B3, B[3], sign);
  _03_FA u_03_fa_2 (.A(A[1]), .B(B1), .Z(n03_fa_1_c), .S(S[1]), .C(n03_fa_2_c));
  _03_FA u_03_fa_3 (.A(A[2]), .B(B2), .Z(n03_fa_2_c), .S(S[2]), .C(n03_fa_3_c));
  _03_FA u_03_fa_4 (.A(A[3]), .B(B3), .Z(n03_fa_3_c), .S(S[3]), .C(C));

  // Notes on the sheet:
  //   0th
  //   1th
  //   2th
  //   3th
endmodule
