// Logisim project JOB06_1411.circ as structural Verilog: 29 circuits, main circuit main
module main (
);

  wire clock_1_out, clock_2_out;

  Clock #(.highDuration(2), .lowDuration(2)) clock_1 (.out(clock_1_out));
  Clock clock_2 (.out(clock_2_out));
  _01_basic_gates u_01_basic_gates_1 (
    .A(clock_1_out), .B(clock_2_out));  // open: Y_and, Y_or, Y_not, Y_nand, Y_nor, Y_xor, Y_xnor, Y_buffer
endmodule

module _01_basic_gates (
  input  A,
  input  B,
  output Y_and,
  output Y_or,
  output Y_not,
  output Y_nand,
  output Y_nor,
  output Y_xor,
  output Y_xnor,
  output Y_buffer
);

  and and_1 (Y_and, A, B);
  or or_1 (Y_or, A, B);
  not not_1 (Y_not, A);
  nand nand_1 (Y_nand, A, B);
  nor nor_1 (Y_nor, A, B);
  xor xor_1 (Y_xor, A, B);
  xnor xnor_1 (Y_xnor, A, B);
  buf buffer_1 (Y_buffer, A);
  LED led_1 (.in(Y_and));
  LED led_2 (.in(Y_or));
  LED led_3 (.in(Y_not));
  LED led_4 (.in(Y_nand));
  LED led_5 (.in(Y_nor));
  LED led_6 (.in(Y_xor));
  LED led_7 (.in(Y_xnor));
  LED led_8 (.in(Y_buffer));

  // Notes on the sheet:
  //   basic logic gates
endmodule

module _02_HA (
  input  A,
  input  B,
  output S,
  output C
);

  xor xor_1 (S, A, B);
  and and_1 (C, A, B);
endmodule

module _03_FA (
  input  A,
  input  B,
  input  Z,
  output S,
  output C
);

  wire n02_ha_1_c, n02_ha_1_s, n02_ha_2_c;

  _02_HA u_02_ha_1 (.A(A), .B(B), .S(n02_ha_1_s), .C(n02_ha_1_c));
  _02_HA u_02_ha_2 (.A(n02_ha_1_s), .B(Z), .S(S), .C(n02_ha_2_c));
  or or_1 (C, n02_ha_2_c, n02_ha_1_c);
endmodule

module _04_Add_4bits (
  input  [3:0] A,
  input  [3:0] B,
  output [3:0] S,
  output C
);

  wire n03_fa_1_p5, n03_fa_2_p5, n03_fa_3_p5;

  // _03_FA 03_fa_1: pin names not known; wires that end beside it: A[0], B[0], 1'b0, S[0], n03_fa_1_p5
  // _03_FA 03_fa_2: pin names not known; wires that end beside it: A[1], B[1], n03_fa_1_p5, S[1], n03_fa_2_p5
  // _03_FA 03_fa_3: pin names not known; wires that end beside it: A[2], B[2], n03_fa_2_p5, S[2], n03_fa_3_p5
  // _03_FA 03_fa_4: pin names not known; wires that end beside it: A[3], B[3], n03_fa_3_p5, S[3], C

  // Notes on the sheet:
  //   0th
  //   1th
  //   2th
  //   3th
endmodule

module _05_HS (
  input  A,
  input  B,
  output D,
  output Br
);

  wire not_1_out;

  xor xor_1 (D, A, B);
  not not_1 (not_1_out, A);
  and and_1 (Br, not_1_out, B);
endmodule

module _06_FS (
  input  A,
  input  B,
  input  Z,
  output S,
  output C
);

  wire n05_hs_1_br, n05_hs_1_d, n05_hs_2_br;

  _05_HS u_05_hs_1 (.A(A), .B(B), .D(n05_hs_1_d), .Br(n05_hs_1_br));
  _05_HS u_05_hs_2 (.A(n05_hs_1_d), .B(Z), .D(S), .Br(n05_hs_2_br));
  or or_1 (C, n05_hs_2_br, n05_hs_1_br);
endmodule

module _07_Sub_4bits (
  input  [3:0] A,
  input  [3:0] B,
  output [3:0] S,
  output C
);

  wire n06_fs_1_c, n06_fs_2_c, n06_fs_3_c;

  _06_FS u_06_fs_1 (.A(A[0]), .B(B[0]), .Z(1'b0), .S(S[0]), .C(n06_fs_1_c));
  _06_FS u_06_fs_2 (.A(A[1]), .B(B[1]), .Z(n06_fs_1_c), .S(S[1]), .C(n06_fs_2_c));
  _06_FS u_06_fs_3 (.A(A[2]), .B(B[2]), .Z(n06_fs_2_c), .S(S[2]), .C(n06_fs_3_c));
  _06_FS u_06_fs_4 (.A(A[3]), .B(B[3]), .Z(n06_fs_3_c), .S(S[3]), .C(C));

  // Other names for the same wires on the sheet: d0 = S[0]; d1 = S[1]; d2 = S[2]; d3 = S[3]

  // Notes on the sheet:
  //   0th
  //   1th
  //   2th
  //   3th
endmodule

module _08_add_sub_4bits (
  input  [3:0] A,
  input  [3:0] B,
  input  sign,
  output [3:0] S,
  output C
);

  wire B0, B1, B2, B3, n03_fa_1_c, n03_fa_2_c, n03_fa_3_c;

  _03_FA u_03_fa_1 (.A(A[0]), .B(B0), .Z(sign), .S(S[0]), .C(n03_fa_1_c));
  xor xor_1 (B0, B[0], sign);
  xor xor_2 (B1, B[1], sign);
  xor xor_3 (B2, B[2], sign);
  xor xor_4 (B3, B[3], sign);
  _03_FA u_03_fa_2 (.A(A[1]), .B(B1), .Z(n03_fa_1_c), .S(S[1]), .C(n03_fa_2_c));
  _03_FA u_03_fa_3 (.A(A[2]), .B(B2), .Z(n03_fa_2_c), .S(S[2]), .C(n03_fa_3_c));
  _03_FA u_03_fa_4 (.A(A[3]), .B(B3), .Z(n03_fa_3_c), .S(S[3]), .C(C));

  // Notes on the sheet:
  //   0th
  //   1th
  //   2th
  //   3th
endmodule

module _09_comp (
  input  A,
  input  B,
  output A_B,
  output A__B,
  output A_B_2,
  output A_B_3
);

  wire not_1_out, not_2_out;

  xnor xnor_1 (A_B, A, B);
  xor xor_1 (A__B, A, B);
  and and_1 (A_B_2, A, not_1_out);
  not not_1 (not_1_out, B);
  not not_2 (not_2_out, A);
  and and_2 (A_B_3, not_2_out, B);
endmodule

module _10_encoder (
  input  D7,
  input  D6,
  input  D5,
  input  D4,
  input  D3,
  input  D2,
  input  D1,
  input  D0,
  output B2,
  output B1,
  output B0
);

  or or_1 (B2, D4, D5, D6, D7);
  or or_2 (B1, D2, D3, D6, D7);
  or or_3 (B0, D1, D3, D5, D7);

  // Notes on the sheet:
  //   B2=D4+D5+D6+D7
  //   B1=D2+D3+D6+D7
  //   B0=D1+D3+D5+D7
endmodule

module _11_decoder (
  input  B2,
  input  B1,
  input  B0,
  output D7,
  output D6,
  output D5,
  output D4,
  output D3,
  output D2,
  output D1,
  output D0
);

  wire not_1_out, not_2_out, not_3_out;

  not not_1 (not_1_out, B2);
  not not_2 (not_2_out, B1);
  not not_3 (not_3_out, B0);
  and and_1 (D7, B2, B1, B0);
  and and_2 (D6, B2, B1, not_3_out);
  and and_3 (D5, B2, not_2_out, B0);
  and and_4 (D4, B2, not_2_out, B0);
  and and_5 (D3, not_1_out, B1, B0);
  and and_6 (D2, not_1_out, B1, not_3_out);
  and and_7 (D1, not_1_out, not_2_out, B0);
  and and_8 (D0, not_1_out, not_2_out, not_3_out);
endmodule

module _12_Mux (
  input  in0,
  input  in1,
  input  in2,
  input  in3,
  input  S1,
  input  S0,
  output MUX
);

  wire and_1_out, and_2_out, and_3_out, and_4_out, not_1_out, not_2_out;

  not not_1 (not_1_out, S1);
  not not_2 (not_2_out, S0);
  and and_1 (and_1_out, in0, not_1_out, not_2_out);
  and and_2 (and_2_out, in1, not_1_out, S0);
  and and_3 (and_3_out, in2, S1, not_2_out);
  and and_4 (and_4_out, in3, S1, S0);
  or or_1 (MUX, and_1_out, and_2_out, and_3_out, and_4_out);
endmodule

module _13_DeMux (
  input  indata,
  input  S1,
  input  S0,
  output out0,
  output out1,
  output out2,
  output out3
);

  wire not_1_out, not_2_out;

  not not_1 (not_1_out, S1);
  not not_2 (not_2_out, S0);
  and and_1 (out0, indata, not_1_out, not_2_out);
  and and_2 (out1, indata, not_1_out, S0);
  and and_3 (out2, indata, S1, not_2_out);
  and and_4 (out3, indata, S1, S0);
endmodule

module _14_latch (
  input  R,
  input  S,
  output Q,
  output Qbar
);

  nor nor_1 (Q, R, Qbar);
  nor nor_2 (Qbar, Q, S);
endmodule

module _15_RSFF (
  input  R,
  input  clk,
  input  S,
  output Q,
  output Qbar
);

  wire and_1_out, and_2_out;

  and and_1 (and_1_out, R, clk);
  and and_2 (and_2_out, clk, S);
  nor nor_1 (Q, and_1_out, Qbar);
  nor nor_2 (Qbar, Q, and_2_out);
endmodule

module _16_JKFF (
  input  K,
  input  clk,
  input  J,
  output Q,
  output Qbar
);

  wire and_1_out, and_2_out;

  and and_1 (and_1_out, K, Q, clk);
  and and_2 (and_2_out, clk, Qbar, J);
  nor nor_1 (Q, and_1_out, Qbar);
  nor nor_2 (Qbar, Q, and_2_out);
endmodule

module _17_DFF (
  input  clk,
  input  D,
  output Q,
  output Qbar
);

  wire and_1_out, and_2_out, not_1_out;

  not not_1 (not_1_out, D);
  and and_1 (and_1_out, not_1_out, Q, clk);
  and and_2 (and_2_out, clk, Qbar, D);
  nor nor_1 (Q, and_1_out, Qbar);
  nor nor_2 (Qbar, Q, and_2_out);
endmodule

module _18_TFF (
  input  clk,
  input  T,
  output Q,
  output Qbar
);

  wire and_1_out, and_2_out;

  and and_1 (and_1_out, T, Q, clk);
  and and_2 (and_2_out, clk, Qbar, T);
  nor nor_1 (Q, and_1_out, Qbar);
  nor nor_2 (Qbar, Q, and_2_out);
endmodule

module _19_test (
  input  in_1,
  input  in_2,
  input  in_3,
  input  in_4,
  input  in_5,
  input  in_6,
  output out_7,
  output out_8,
  output out_9,
  output out_10
);

  wire clock_1_out, clock_2_out, clock_3_out, clock_4_out;

  Clock clock_1 (.out(clock_1_out));
  Clock clock_2 (.out(clock_2_out));
  S_R_Flip_Flop s_r_ff_1 (.S(in_1), .clk(clock_1_out), .R(in_3), .Q(out_7));  // open: Qn, preset, reset
  D_Flip_Flop d_ff_1 (.clk(clock_2_out), .D(in_5), .Q(out_9));  // open: Qn, preset, reset
  Clock clock_3 (.out(clock_3_out));
  Clock clock_4 (.out(clock_4_out));
  J_K_Flip_Flop j_k_ff_1 (.J(in_2), .clk(clock_3_out), .K(in_4), .Q(out_8));  // open: Qn, preset, reset
  T_Flip_Flop t_ff_1 (.clk(clock_4_out), .T(in_6), .Q(out_10));  // open: Qn, preset, reset
endmodule

module _20_siso (
  input  indata,
  output outdata
);

  wire clk_out, d_ff_1_q, d_ff_2_q, d_ff_3_q;

  Clock clk (.out(clk_out));
  D_Flip_Flop d_ff_1 (.clk(clk_out), .D(indata), .Q(d_ff_1_q));  // open: Qn, preset, reset
  D_Flip_Flop d_ff_2 (.clk(clk_out), .D(d_ff_1_q), .Q(d_ff_2_q));  // open: Qn, preset, reset
  D_Flip_Flop d_ff_3 (.clk(clk_out), .D(d_ff_2_q), .Q(d_ff_3_q));  // open: Qn, preset, reset
  D_Flip_Flop d_ff_4 (.clk(clk_out), .D(d_ff_3_q), .Q(outdata));  // open: Qn, preset, reset

  // Notes on the sheet:
  //   A
  //   B
  //   C
  //   D
endmodule

module _21_sipo (
  input  indata,
  output out0,
  output out1,
  output out2,
  output out3
);

  wire clk_out;

  Clock clk (.out(clk_out));
  D_Flip_Flop d_ff_1 (.clk(clk_out), .D(indata), .Q(out0));  // open: Qn, preset, reset
  D_Flip_Flop d_ff_2 (.clk(clk_out), .D(out0), .Q(out1));  // open: Qn, preset, reset
  D_Flip_Flop d_ff_3 (.clk(clk_out), .D(out1), .Q(out2));  // open: Qn, preset, reset
  D_Flip_Flop d_ff_4 (.clk(clk_out), .D(out2), .Q(out3));  // open: Qn, preset, reset

  // Notes on the sheet:
  //   A
  //   B
  //   C
  //   D
endmodule

module _22_piso (
  input  in0,
  input  in1,
  input  in2,
  input  in3,
  input  shift___load_bar,
  output D
);

  wire and_1_out, and_2_out, and_3_out, and_4_out, and_5_out, and_6_out, clk_out, d_ff_1_q, d_ff_2_q,
       d_ff_3_q, not_1_out, or_1_out, or_2_out, or_3_out;

  not not_1 (not_1_out, shift___load_bar);
  Clock clk (.out(clk_out));
  and and_1 (and_1_out, d_ff_1_q, shift___load_bar);
  or or_1 (or_1_out, and_1_out, and_2_out);
  D_Flip_Flop d_ff_1 (.clk(clk_out), .D(in0), .Q(d_ff_1_q));  // open: Qn, preset, reset
  and and_2 (and_2_out, not_1_out, in1);
  and and_3 (and_3_out, d_ff_2_q, shift___load_bar);
  and and_4 (and_4_out, not_1_out, in2);
  or or_2 (or_2_out, and_3_out, and_4_out);
  D_Flip_Flop d_ff_2 (.clk(clk_out), .D(or_1_out), .Q(d_ff_2_q));  // open: Qn, preset, reset
  D_Flip_Flop d_ff_3 (.clk(clk_out), .D(or_2_out), .Q(d_ff_3_q));  // open: Qn, preset, reset
  and and_5 (and_5_out, d_ff_3_q, shift___load_bar);
  and and_6 (and_6_out, not_1_out, in3);
  or or_3 (or_3_out, and_5_out, and_6_out);
  D_Flip_Flop d_ff_4 (.clk(clk_out), .D(or_3_out), .Q(D));  // open: Qn, preset, reset

  // Notes on the sheet:
  //   A
  //   B
  //   C
endmodule

module _23_pipo (
  input  in0,
  input  in1,
  input  in2,
  input  in3,
  output out0,
  output out1,
  output out2,
  output out3
);

  wire clk_out;

  Clock clk (.out(clk_out));
  D_Flip_Flop d_ff_1 (.clk(clk_out), .D(in0), .Q(out0));  // open: Qn, preset, reset
  D_Flip_Flop d_ff_2 (.clk(clk_out), .D(in1), .Q(out1));  // open: Qn, preset, reset
  D_Flip_Flop d_ff_3 (.clk(clk_out), .D(in2), .Q(out2));  // open: Qn, preset, reset
  D_Flip_Flop d_ff_4 (.clk(clk_out), .D(in3), .Q(out3));  // open: Qn, preset, reset

  // Notes on the sheet:
  //   A
  //   B
  //   C
  //   D
endmodule

module _24_recirc (
  input  control,
  input  indata,
  output outdata
);

  wire and_1_out, and_2_out, clk_out, d_ff_1_q, d_ff_2_q, d_ff_3_q, not_1_out, or_1_out;

  not not_1 (not_1_out, control);
  and and_1 (and_1_out, outdata, not_1_out);
  and and_2 (and_2_out, control, indata);
  or or_1 (or_1_out, and_1_out, and_2_out);
  Clock clk (.out(clk_out));
  D_Flip_Flop d_ff_1 (.clk(clk_out), .D(or_1_out), .Q(d_ff_1_q));  // open: Qn, preset, reset
  D_Flip_Flop d_ff_2 (.clk(clk_out), .D(d_ff_1_q), .Q(d_ff_2_q));  // open: Qn, preset, reset
  D_Flip_Flop d_ff_3 (.clk(clk_out), .D(d_ff_2_q), .Q(d_ff_3_q));  // open: Qn, preset, reset
  D_Flip_Flop d_ff_4 (.clk(clk_out), .D(d_ff_3_q), .Q(outdata));  // open: Qn, preset, reset

  // Notes on the sheet:
  //   A
  //   B
  //   C
  //   D
endmodule

module _25_async_down_counter (
);

  wire clk_out;
  wire [3:0] j_k_ff_1_q;

  Clock clk (.out(clk_out));
  J_K_Flip_Flop j_k_ff_1 (.J(1'b1), .clk(clk_out), .K(1'b1), .Q(j_k_ff_1_q[0]));  // open: Qn, preset, reset
  J_K_Flip_Flop j_k_ff_2 (.J(1'b1), .clk(j_k_ff_1_q[0]), .K(1'b1), .Q(j_k_ff_1_q[1]));  // open: Qn, preset, reset
  J_K_Flip_Flop j_k_ff_3 (.J(1'b1), .clk(j_k_ff_1_q[1]), .K(1'b1), .Q(j_k_ff_1_q[2]));  // open: Qn, preset, reset
  J_K_Flip_Flop j_k_ff_4 (.J(1'b1), .clk(j_k_ff_1_q[2]), .K(1'b1), .Q(j_k_ff_1_q[3]));  // open: Qn, preset, reset
  Hex_Digit_Display hex_digit_display_1 (.value(j_k_ff_1_q));  // open: dp

  // Notes on the sheet:
  //   A
  //   B
  //   C
  //   D
endmodule

module _26_async_up_counter (
);

  wire clk_out;
  wire [3:0] j_k_ff_1_q;

  Clock clk (.out(clk_out));
  J_K_Flip_Flop #(.trigger("falling")) j_k_ff_1 (
    .J(1'b1), .clk(clk_out), .K(1'b1), .Q(j_k_ff_1_q[0]));  // open: Qn, preset, reset
  J_K_Flip_Flop #(.trigger("falling")) j_k_ff_2 (
    .J(1'b1), .clk(j_k_ff_1_q[0]), .K(1'b1), .Q(j_k_ff_1_q[1]));  // open: Qn, preset, reset
  J_K_Flip_Flop #(.trigger("falling")) j_k_ff_3 (
    .J(1'b1), .clk(j_k_ff_1_q[1]), .K(1'b1), .Q(j_k_ff_1_q[2]));  // open: Qn, preset, reset
  J_K_Flip_Flop #(.trigger("falling")) j_k_ff_4 (
    .J(1'b1), .clk(j_k_ff_1_q[2]), .K(1'b1), .Q(j_k_ff_1_q[3]));  // open: Qn, preset, reset
  Hex_Digit_Display hex_digit_display_1 (.value(j_k_ff_1_q));  // open: dp

  // Notes on the sheet:
  //   A
  //   B
  //   C
  //   D
endmodule

module _27_sync_8_counter (
);

  wire and_1_out, clk_out;
  wire [2:0] j_k_ff_1_q;

  Clock clk (.out(clk_out));
  J_K_Flip_Flop #(.trigger("falling")) j_k_ff_1 (
    .J(1'b1), .clk(clk_out), .K(1'b1), .Q(j_k_ff_1_q[0]));  // open: Qn, preset, reset
  J_K_Flip_Flop #(.trigger("falling")) j_k_ff_2 (
    .J(j_k_ff_1_q[0]), .clk(clk_out), .K(j_k_ff_1_q[0]), .Q(j_k_ff_1_q[1]));  // open: Qn, preset, reset
  and and_1 (and_1_out, j_k_ff_1_q[0], j_k_ff_1_q[1]);
  J_K_Flip_Flop #(.trigger("falling")) j_k_ff_3 (
    .J(and_1_out), .clk(clk_out), .K(and_1_out), .Q(j_k_ff_1_q[2]));  // open: Qn, preset, reset
  Hex_Digit_Display hex_digit_display_1 (.value({1'b0, j_k_ff_1_q}));  // open: dp
endmodule

module _28_ring_counter (
);

  wire clock_1_out, d_ff_1_q, d_ff_2_q, d_ff_3_q, d_ff_4_q;

  Clock clock_1 (.out(clock_1_out));
  D_Flip_Flop d_ff_1 (.clk(clock_1_out), .D(d_ff_4_q), .Q(d_ff_1_q));  // open: Qn, preset, reset
  D_Flip_Flop d_ff_2 (.clk(clock_1_out), .D(d_ff_1_q), .Q(d_ff_2_q));  // open: Qn, preset, reset
  D_Flip_Flop d_ff_3 (.clk(clock_1_out), .D(d_ff_2_q), .Q(d_ff_3_q));  // open: Qn, preset, reset
  D_Flip_Flop d_ff_4 (.clk(clock_1_out), .D(d_ff_3_q), .Q(d_ff_4_q));  // open: Qn, preset, reset
endmodule
